# Fritzing sketch esp8266_programmer (saved by Fritzing 0.8.5b)
breadboards: 1

parts:
  C1 = Ceramic Capacitor [capacitance=1µF package="100 mil [THT, multilayer]"]
  C2 = Electrolytic Capacitor [capacitance=10µF package="100 mil [THT, electrolytic]"]
  U5 = Mystery Part - 4 pins [chip_label="USB TTL" package=THT]
  U7 = Mystery Part - 8 pins [chip_label=ESP8266 package=THT]
  DS4 = DS18B20 1-Wire Temperature Sensor [part_number=DS18B20]
  LED1 = LED - 5mm [color="Red (633nm)" package="5 mm [THT]"]
  R1 = Resistor [tolerance=±5% resistance=100 package=THT]
  S1 = Pushbutton [package="[THT]"]
  R2 = Resistor [tolerance=±5% resistance=10k package=THT]
  S2 = Pushbutton [package="[THT]"]
  R3 = Resistor [tolerance=±5% resistance=10k package=THT]
  R4 = Resistor [tolerance=±5% resistance=4.7k package=THT]
  U9 = mystery part, 3 pins [chip_label=MCP170]
  C3 = Ceramic Capacitor [capacitance=1µF package="100 mil [THT, multilayer]"]

nets:
  GND: C1.0, C2.-, U5.GND, U7.GND, DS4.GND, S1.Pin_1, S1.Pin_2, S2.Pin_1, S2.Pin_2, U9.pin1, C3.0
  N1: C1.1, C2.+, U5.5V, U9.pin2
  N2: U5.TX, U7.TXO
  N3: U5.RX, U7.RXI
  N4: U7.CHPD/Enable, U7.3.3V, R1.Pin_1, U9.pin3, C3.1
  N5: U7.RST, S2.Pin_3, S2.Pin_4, R3.Pin_1
  N6: U7.GPIO0, DS4.DQ, S1.Pin_3, S1.Pin_4, R2.Pin_1, R4.Pin_1
  N7: U7.GPIO2, LED1.cathode
  N8: DS4.VDD, R3.Pin_0, R4.Pin_0
  N9: LED1.anode, R1.Pin_0

custom parts:
  Mystery Part - 4 pins: A dummy, proxy, ersatz, stand-in part for whatever you want. With 4 pins on a 100 mil inline pin header footprint.
  Mystery Part - 8 pins: A dummy, proxy, ersatz, stand-in part for whatever you want. With 8 pins on a 300mil inline pin header footprint.
