# Fritzing sketch sensor_controller_battery (saved by Fritzing 0.8.5b)
breadboards: 2

parts:
  VCC1 = Battery
  U6 = Mystery Part - 8 pins [chip_label=ESP8266 package=THT]
  U7 = attiny85 [package=dip]
  DS5 = DS18B20 1-Wire Temperature Sensor [part_number=DS18B20]
  R27 = Resistor [tolerance=±5% resistance=4.7k package=THT]
  Q8 = Basic FET N-Channel [package="TO220 [THT]"]
  D14 = Rectifier Diode [part_number=1N4001 package="Melf DO-213 AB [SMD]"]  # not connected
  C4 = Ceramic Capacitor [capacitance=1µF package="100 mil [THT, multilayer]"]
  R28 = Resistor [tolerance=±5% resistance=10k package=THT]
  R29 = Resistor [tolerance=±5% resistance=10k package=THT]
  C6 = Ceramic Capacitor [capacitance=1µF package="100 mil [THT, multilayer]"]
  U8 = mystery part, 3 pins [chip_label=MCP170]
  R31 = Resistor [tolerance=±5% resistance=10k package=THT]
  C7 = Electrolytic Capacitor [capacitance=10µF package="100 mil [THT, electrolytic]"]
  C8 = Electrolytic Capacitor [capacitance=10µF package="100 mil [THT, electrolytic]"]
  U9 = Mystery Part - 8 pins [chip_label=ESP8266 package=THT]
  R32 = Resistor [tolerance=±5% resistance=4.7k package=THT]
  DS6 = DS18B20 1-Wire Temperature Sensor [part_number=DS18B20]
  VCC2 = Battery
  U10 = attiny85 [package=dip]
  Q9 = Basic FET N-Channel [package="TO220 [THT]"]
  D15 = Rectifier Diode [part_number=1N4001 package="Melf DO-213 AB [SMD]"]
  C9 = Ceramic Capacitor [capacitance=1µF package="100 mil [THT, multilayer]"]
  C10 = Ceramic Capacitor [capacitance=1µF package="100 mil [THT, multilayer]"]
  U11 = mystery part, 3 pins [chip_label=MCP170]
  R33 = Resistor [tolerance=±5% resistance=10k package=THT]
  R34 = Resistor [tolerance=±5% resistance=10k package=THT]
  R35 = Resistor [tolerance=±5% resistance=10k package=THT]

nets:
  N1: VCC1.-, U7.Pin_4, Q8.source, C4.0, C6.0, U8.pin1, R31.Pin_1, C7.-
  N2: VCC1.+, C6.1, U8.pin2, C7.+
  3.3V: U6.CHPD/Enable, U6.3.3V, U7.Pin_8, DS5.VDD, R27.Pin_0, C4.1, R28.Pin_1, R29.Pin_1, U8.pin3
  N3: U6.RST, U7.Pin_2, R28.Pin_0
  N4: U6.GPIO0, DS5.DQ, R27.Pin_1
  N5: U6.GPIO2, U7.Pin_7
  GND: U6.GND, DS5.GND, Q8.drain
  N6: U7.Pin_1, R29.Pin_0
  N7: U7.Pin_6, Q8.gate, R31.Pin_0
  N8: C8.-, VCC2.-, U10.Pin_4, Q9.source, C9.0, C10.0, U11.pin1, R34.Pin_1
  N9: C8.+, VCC2.+, C9.1, U11.pin2
  3.3V_2: U9.CHPD/Enable, U9.3.3V, R32.Pin_0, DS6.VDD, U10.Pin_8, D15.cathode, C10.1, U11.pin3, R33.Pin_1, R35.Pin_1
  N10: U9.RST, U10.Pin_2, R35.Pin_0
  N11: U9.GPIO0, R32.Pin_1, DS6.DQ
  N12: U9.GPIO2, U10.Pin_7
  GND_2: U9.GND, DS6.GND, Q9.drain, D15.anode
  N13: U10.Pin_6, Q9.gate, R34.Pin_0

notes:
  Only needed for (1,7)

custom parts:
  Mystery Part - 8 pins: A dummy, proxy, ersatz, stand-in part for whatever you want. With 8 pins on a 300mil inline pin header footprint.
